# Fritzing sketch garrafa_termica (saved by Fritzing 0.9.3b)
breadboards: 1

parts:
  J1 = Peltier Element
  VCC1 = Battery block 9V
  Placa_Arduino_Uno_R4 = Arduino Uno (Rev3)
  R4 = Resistor [tolerance=±5% resistance=1k package=THT]
  R5 = Resistor [tolerance=±5% resistance=2.2k package=THT]
  Módulo_Bluetooth_HC-6 = Bluetooth HC-05 Macho
  Relay1 = Keyes Relay [package=THT]
  S1 = Pushbutton [package="[THT]"]
  R6 = Resistor [tolerance=±5% resistance=1k package=THT]

nets:
  N1: J1.pin2, Relay1.NO
  N2: VCC1.-, Relay1.C
  N3: Placa_Arduino_Uno_R4.D8, Relay1.signal
  N4: Placa_Arduino_Uno_R4.D0/RX, Módulo_Bluetooth_HC-6.TXD
  N5: Placa_Arduino_Uno_R4.D1/TX, R4.Pin_0
  N6: Placa_Arduino_Uno_R4.D7, S1.Pin_1, S1.Pin_2, R6.Pin_0
  5V: Placa_Arduino_Uno_R4.5V, Módulo_Bluetooth_HC-6.VCC, Relay1.power
  GND: Placa_Arduino_Uno_R4.GND, R5.Pin_1, Módulo_Bluetooth_HC-6.GND, Relay1.ground, S1.Pin_3, S1.Pin_4, R6.Pin_1
  N7: R4.Pin_1, R5.Pin_0, Módulo_Bluetooth_HC-6.RXD

custom parts:
  Keyes Relay: The Keyes 5V relay module is suitable for SCM development, home appliance control. It uses a 5V~12V TIL control signal which can control DC / AC signal.
